// Logisim project branch-comp.circ as structural Verilog: 1 circuit, main circuit branch_comp
module branch_comp (
  input  [31:0] BrData1,
  input  [31:0] BrData2,
  input  BrUn,
  output BrEq,
  output BrLt
);

  wire Eq_signed, Eq_unsigned, Lt_signed, Lt_unsigned;

  Comparator #(.width(32)) comparator_1 (.a(BrData1), .b(BrData2), .eq(Eq_signed));  // open: gt, lt
  Comparator #(.mode("unsigned"), .width(32)) comparator_2 (
    .a(BrData1), .b(BrData2), .eq(Eq_unsigned));  // open: gt, lt
  Comparator #(.width(32)) comparator_3 (.a(BrData1), .b(BrData2), .lt(Lt_signed));  // open: gt, eq
  Comparator #(.mode("unsigned"), .width(32)) comparator_4 (
    .a(BrData1), .b(BrData2), .lt(Lt_unsigned));  // open: gt, eq
  Multiplexer multiplexer_1 (.in0(Eq_signed), .in1(Eq_unsigned), .out(BrEq), .sel(BrUn));
  Multiplexer multiplexer_2 (.in0(Lt_signed), .in1(Lt_unsigned), .out(BrLt), .sel(BrUn));

  // Notes on the sheet:
  //   INPUTS to your circuit
  //   DON'T CHANGE THE LOCATIONS OF THE INPUTS AND OUTPUTS!
  //   OUTPUT from your circuit
endmodule
