// Logisim project cpu.circ as structural Verilog: 1 circuit, main circuit cpu
module cpu (
  input  clk,
  input  [31:0] Instruction,
  input  [31:0] MemReadData,
  output [31:0] MemAddress,
  output [31:0] ProgramCounter,
  output [31:0] ra,
  output [31:0] sp,
  output [31:0] t0,
  output [31:0] t1,
  output [31:0] t2,
  output [31:0] s0,
  output [31:0] s1,
  output [31:0] a0,
  output [3:0] MemWriteMask,
  output [31:0] MemWriteData
);

  wire ASel, BrEq, BrLt, BrUn, BSel, comparator_3_eq, comparator_4_eq, comparator_5_eq, comparator_6_eq,
       comparator_7_eq, comparator_8_eq, comparator_9_eq, comparator_10_eq, comparator_11_eq,
       comparator_12_eq, comparator_13_eq, comparator_14_eq, comparator_17_eq, comparator_18_eq,
       comparator_19_eq, comparator_20_eq, comparator_21_eq, comparator_22_eq, comparator_23_eq,
       comparator_24_eq, comparator_25_eq, comparator_26_eq, comparator_27_eq, comparator_28_eq,
       comparator_29_eq, comparator_30_eq, comparator_31_eq, comparator_32_eq, comparator_33_gt,
       comparator_34_eq, comparator_35_eq, comparator_36_gt, comparator_37_eq, comparator_38_eq,
       comparator_39_gt, comparator_40_eq, Forward_rs2, is_ALUForwardA, is_ALUForwardB, is_imm,
       is_MemForwardA, is_MemForwardB, is_PC, is_ReadData1, is_ReadData2, LoadStall_Control, nor_1_out,
       nor_2_out, not_1_out, not_2_out, not_3_out, not_4_out, not_5_out, or_1_out, or_2_out, or_3_out,
       or_4_out, or_6_out, or_7_out, PCSel_IF, WBForward_rs1, WBForward_rs2;
  wire [1:0] ForwardA_Control, ForwardB_Control;
  wire [2:0] funct3;
  wire [3:0] ALUSel;
  wire [6:0] funct7;
  wire [14:0] Control, Control_EX, Control_MEM, Control_WB, multiplexer_8_out;
  wire [24:0] Instruction_ID;
  wire [31:0] ALUResult, Immediate, Instruction_EX, Instruction_IF, Instruction_MEM, Instruction_WB,
       LoadData, multiplexer_1_out, multiplexer_5_out, multiplexer_6_out, multiplexer_7_out,
       multiplexer_9_out, multiplexer_11_out, multiplexer_12_out, NextPC, NextPC_EX, NextPC_ID, NextPC_MEM,
       PC_EX, PC_ID, ReadData1, ReadData1_EX, ReadData2, ReadData2_EX, Select_NextPC, SelectInstruction,
       WriteBack, WriteBack_ID, WriteData_EX, WriteData_MEM;

  Adder #(.width(32)) adder_1 (.a(ProgramCounter), .b(32'h4), .out(NextPC));  // open: cin, cout
  or or_1 (or_1_out, Control_EX[0], PCSel_IF);
  Multiplexer #(.width(32)) multiplexer_1 (
    .in0(Select_NextPC), .in1(MemAddress), .out(multiplexer_1_out), .sel(PCSel_IF));
  Multiplexer #(.width(32)) multiplexer_2 (
    .in0(NextPC), .in1(ProgramCounter), .out(Select_NextPC), .sel(LoadStall_Control));
  Multiplexer #(.width(32)) multiplexer_3 (.in0(Instruction), .in1(32'h13), .out(SelectInstruction), .sel(or_1_out));
  Register #(.width(32)) PC (.D(multiplexer_1_out), .clk(clk), .Q(ProgramCounter));  // open: en, clr
  Comparator #(.mode("unsigned"), .width(1)) comparator_1 (.a(ASel), .b(1'b0), .eq(is_ReadData1));  // open: gt, lt
  Comparator #(.mode("unsigned"), .width(1)) comparator_2 (.a(ASel), .b(1'b1), .eq(is_PC));  // open: gt, lt
  not not_1 (not_1_out, comparator_3_eq);
  Comparator #(.mode("unsigned"), .width(5)) comparator_3 (
    .a(Instruction_WB[11:7]), .b({5{1'b0}}), .eq(comparator_3_eq));  // open: gt, lt
  Comparator #(.mode("unsigned"), .width(5)) comparator_4 (
    .a(Instruction_WB[11:7]), .b(Instruction_EX[19:15]), .eq(comparator_4_eq));  // open: gt, lt
  Comparator #(.mode("unsigned"), .width(7)) comparator_5 (
    .a(Instruction_EX[6:0]), .b(7'b0100011), .eq(comparator_5_eq));  // open: gt, lt
  Comparator #(.mode("unsigned"), .width(7)) comparator_6 (
    .a(Instruction_EX[6:0]), .b(7'b1100011), .eq(comparator_6_eq));  // open: gt, lt
  Comparator #(.mode("unsigned"), .width(7)) comparator_7 (
    .a(Instruction_MEM[6:0]), .b(7'b0110011), .eq(comparator_7_eq));  // open: gt, lt
  Comparator #(.mode("unsigned"), .width(7)) comparator_8 (
    .a(Instruction_MEM[6:0]), .b(7'b0010011), .eq(comparator_8_eq));  // open: gt, lt
  Comparator #(.mode("unsigned"), .width(7)) comparator_9 (
    .a(Instruction_MEM[6:0]), .b(7'b0110111), .eq(comparator_9_eq));  // open: gt, lt
  Comparator #(.mode("unsigned"), .width(7)) comparator_10 (
    .a(Instruction_EX[6:0]), .b(7'b0110011), .eq(comparator_10_eq));  // open: gt, lt
  Comparator #(.mode("unsigned"), .width(7)) comparator_11 (
    .a(Instruction_EX[6:0]), .b(7'b0010011), .eq(comparator_11_eq));  // open: gt, lt
  Comparator #(.mode("unsigned"), .width(7)) comparator_12 (
    .a(Instruction_EX[6:0]), .b(7'b1100111), .eq(comparator_12_eq));  // open: gt, lt
  nor nor_1 (nor_1_out, comparator_5_eq, comparator_6_eq);
  not not_2 (not_2_out, comparator_13_eq);
  Comparator #(.mode("unsigned"), .width(5)) comparator_13 (
    .a(Instruction_MEM[11:7]), .b({5{1'b0}}), .eq(comparator_13_eq));  // open: gt, lt
  Comparator #(.mode("unsigned"), .width(5)) comparator_14 (
    .a(Instruction_MEM[11:7]), .b(Instruction_EX[19:15]), .eq(comparator_14_eq));  // open: gt, lt
  or or_2 (or_2_out, comparator_10_eq, comparator_11_eq, comparator_12_eq);
  Multiplexer #(.width(32)) multiplexer_4 (
    .in0(SelectInstruction), .in1({funct7, Instruction_ID[24:15], funct3, Instruction_ID[11:0]}),
    .out(Instruction_IF), .sel(LoadStall_Control));
  and and_1 (is_MemForwardA, Control_WB[1], not_1_out, comparator_4_eq, nor_1_out);
  or or_3 (or_3_out, comparator_7_eq, comparator_8_eq, comparator_9_eq);
  and and_2 (is_ALUForwardA, or_3_out, not_2_out, comparator_14_eq, or_2_out);
  Register #(.width(32)) register_1 (.D(Select_NextPC), .clk(clk), .Q(NextPC_ID));  // open: en, clr
  Register #(.width(32)) register_2 (.D(multiplexer_5_out), .clk(clk), .Q(PC_ID));  // open: en, clr
  Multiplexer #(.width(32)) multiplexer_5 (
    .in0(ProgramCounter), .in1(PC_ID), .out(multiplexer_5_out), .sel(LoadStall_Control));
  Register #(.width(32)) register_3 (
    .D(Instruction_IF), .clk(clk), .Q({funct7, Instruction_ID[24:15], funct3, Instruction_ID[11:0]}));  // open: en, clr
  Priority_Encoder #(.select_enc(2)) priority_encoder_1 (
    .in0(is_ReadData1), .in1(is_PC), .in2(is_MemForwardA), .in3(is_ALUForwardA), .out(ForwardA_Control));  // open: gs, en_out, en_in
  Comparator #(.mode("unsigned"), .width(1)) comparator_15 (.a(BSel), .b(1'b0), .eq(is_ReadData2));  // open: gt, lt
  Comparator #(.mode("unsigned"), .width(1)) comparator_16 (.a(BSel), .b(1'b1), .eq(is_imm));  // open: gt, lt
  not not_3 (not_3_out, comparator_17_eq);
  Comparator #(.mode("unsigned"), .width(5)) comparator_17 (
    .a(Instruction_WB[11:7]), .b({5{1'b0}}), .eq(comparator_17_eq));  // open: gt, lt
  Comparator #(.mode("unsigned"), .width(5)) comparator_18 (
    .a(Instruction_WB[11:7]), .b(Instruction_EX[24:20]), .eq(comparator_18_eq));  // open: gt, lt
  Comparator #(.mode("unsigned"), .width(7)) comparator_19 (
    .a(Instruction_EX[6:0]), .b(7'b0100011), .eq(comparator_19_eq));  // open: gt, lt
  Comparator #(.mode("unsigned"), .width(7)) comparator_20 (
    .a(Instruction_EX[6:0]), .b(7'b1100011), .eq(comparator_20_eq));  // open: gt, lt
  Comparator #(.mode("unsigned"), .width(7)) comparator_21 (
    .a(Instruction_MEM[6:0]), .b(7'b0110011), .eq(comparator_21_eq));  // open: gt, lt
  Comparator #(.mode("unsigned"), .width(7)) comparator_22 (
    .a(Instruction_MEM[6:0]), .b(7'b0010011), .eq(comparator_22_eq));  // open: gt, lt
  Comparator #(.mode("unsigned"), .width(7)) comparator_23 (
    .a(Instruction_MEM[6:0]), .b(7'b0110111), .eq(comparator_23_eq));  // open: gt, lt
  not not_4 (not_4_out, comparator_24_eq);
  Comparator #(.mode("unsigned"), .width(5)) comparator_24 (
    .a(Instruction_MEM[11:7]), .b({5{1'b0}}), .eq(comparator_24_eq));  // open: gt, lt
  Comparator #(.mode("unsigned"), .width(5)) comparator_25 (
    .a(Instruction_MEM[11:7]), .b(Instruction_EX[24:20]), .eq(comparator_25_eq));  // open: gt, lt
  Comparator #(.mode("unsigned"), .width(7)) comparator_26 (
    .a(Instruction_EX[6:0]), .b(7'b0110011), .eq(comparator_26_eq));  // open: gt, lt
  Comparator #(.mode("unsigned"), .width(7)) comparator_27 (
    .a(Instruction_EX[6:0]), .b(7'b0010011), .eq(comparator_27_eq));  // open: gt, lt
  regfile regfile_1 (
    .ReadIndex1(Instruction_ID[19:15]), .ReadIndex2(Instruction_ID[24:20]),
    .WriteIndex(Instruction_WB[11:7]), .WriteData(WriteBack_ID), .RegWEn(Control_WB[1]), .clk(clk), .ra(ra),
    .sp(sp), .t0(t0), .t1(t1), .t2(t2), .s0(s0), .s1(s1), .a0(a0), .ReadData1(ReadData1),
    .ReadData2(ReadData2));
  and and_3 (is_MemForwardB, Control_WB[1], not_3_out, comparator_18_eq, nor_2_out);
  nor nor_2 (nor_2_out, comparator_19_eq, comparator_20_eq);
  or or_4 (or_4_out, comparator_21_eq, comparator_22_eq, comparator_23_eq);
  or or_5 (comparator_25_eq, comparator_26_eq, comparator_27_eq);
  and and_4 (is_ALUForwardB, or_4_out, not_4_out, comparator_25_eq, comparator_25_eq);
  Multiplexer #(.width(32)) multiplexer_6 (
    .in0(ReadData1), .in1(WriteBack_ID), .out(multiplexer_6_out), .sel(WBForward_rs1));
  Multiplexer #(.width(32)) multiplexer_7 (
    .in0(ReadData2), .in1(WriteBack_ID), .out(multiplexer_7_out), .sel(WBForward_rs2));
  Multiplexer #(.width(15)) multiplexer_8 (
    .in0(Control), .in1({15{1'b0}}), .out(multiplexer_8_out), .sel(LoadStall_Control));
  Multiplexer #(.width(32)) multiplexer_9 (
    .in0({funct7, Instruction_ID[24:15], funct3, Instruction_ID[11:0]}), .in1(32'h13),
    .out(multiplexer_9_out), .sel(or_6_out));
  or or_6 (or_6_out, LoadStall_Control, Control_EX[0]);
  Register #(.width(32)) register_4 (.D(NextPC_ID), .clk(clk), .Q(NextPC_EX));  // open: en, clr
  Register #(.width(32)) register_5 (.D(PC_ID), .clk(clk), .Q(PC_EX));  // open: en, clr
  Register #(.width(32)) register_6 (.D(multiplexer_6_out), .clk(clk), .Q(ReadData1_EX));  // open: en, clr
  Register #(.width(32)) register_7 (.D(multiplexer_7_out), .clk(clk), .Q(ReadData2_EX));  // open: en, clr
  Register #(.width(15)) register_8 (
    .D(multiplexer_8_out), .clk(clk), .Q({Control_EX[14:12], ALUSel, BSel, ASel, BrUn, Control_EX[4:0]}));  // open: en, clr
  Register #(.width(32)) register_9 (.D(multiplexer_9_out), .clk(clk), .Q(Instruction_EX));  // open: en, clr
  Priority_Encoder #(.select_enc(2)) priority_encoder_2 (
    .in0(is_ReadData2), .in1(is_imm), .in2(is_MemForwardB), .in3(is_ALUForwardB), .out(ForwardB_Control));  // open: gs, en_out, en_in
  Multiplexer #(.width(32)) multiplexer_10 (
    .in0(ReadData2_EX), .in1(MemAddress), .out(WriteData_EX), .sel(Forward_rs2));
  control_logic control_logic_1 (
    .Instruction(Instruction_EX), .BrEq(BrEq), .BrLt(BrLt), .PCSel(Control_EX[0]), .RegWEn(Control_EX[1]),
    .ImmSel(Control_EX[4:2]), .BrUn(BrUn), .ASel(ASel), .BSel(BSel), .ALUSel(ALUSel), .MemRW(Control_EX[12]),
    .WBSel(Control_EX[14:13]));
  Comparator #(.mode("unsigned"), .width(5)) comparator_28 (
    .a(Instruction_EX[11:7]), .b({5{1'b0}}), .eq(comparator_28_eq));  // open: gt, lt
  Comparator #(.mode("unsigned"), .width(5)) comparator_29 (
    .a(Instruction_EX[11:7]), .b(Instruction_ID[19:15]), .eq(comparator_29_eq));  // open: gt, lt
  Comparator #(.mode("unsigned"), .width(5)) comparator_30 (
    .a(Instruction_EX[11:7]), .b(Instruction_ID[24:20]), .eq(comparator_30_eq));  // open: gt, lt
  Multiplexer #(.select(2), .width(32)) multiplexer_11 (
    .in0(ReadData1_EX), .in1(PC_EX), .in2(WriteBack_ID), .in3(MemAddress), .out(multiplexer_11_out),
    .sel(ForwardA_Control));
  Multiplexer #(.select(2), .width(32)) multiplexer_12 (
    .in0(ReadData2_EX), .in1(Immediate), .in2(WriteBack_ID), .in3(MemAddress), .out(multiplexer_12_out),
    .sel(ForwardB_Control));
  Comparator #(.mode("unsigned"), .width(7)) comparator_31 (
    .a(Instruction_EX[6:0]), .b(7'b0000011), .eq(comparator_31_eq));  // open: gt, lt
  not not_5 (not_5_out, comparator_28_eq);
  or or_7 (or_7_out, comparator_29_eq, comparator_30_eq);
  and and_5 (LoadStall_Control, comparator_31_eq, not_5_out, or_7_out);
  alu alu_1 (.A(multiplexer_11_out), .B(multiplexer_12_out), .ALUSel(ALUSel), .ALUResult(ALUResult));
  branch_comp branch_comp_1 (.BrData1(ReadData1_EX), .BrData2(ReadData2_EX), .BrUn(BrUn), .BrEq(BrEq), .BrLt(BrLt));
  imm_gen imm_gen_1 (.Instruction(Instruction_EX), .ImmSel(Control_EX[4:2]), .Immediate(Immediate));
  Register #(.width(32)) register_10 (.D(NextPC_EX), .clk(clk), .Q(NextPC_MEM));  // open: en, clr
  Register #(.width(32)) register_11 (.D(ALUResult), .clk(clk), .Q(MemAddress));  // open: en, clr
  Register #(.width(32)) register_12 (.D(WriteData_EX), .clk(clk), .Q(WriteData_MEM));  // open: en, clr
  Register #(.width(32)) register_13 (.D(Instruction_EX), .clk(clk), .Q(Instruction_MEM));  // open: en, clr
  Register #(.width(15)) register_14 (
    .D({Control_EX[14:12], ALUSel, BSel, ASel, BrUn, Control_EX[4:0]}), .clk(clk), .Q(Control_MEM));  // open: en, clr
  Register #(.width(1)) register_15 (.D(Control_EX[0]), .clk(clk), .Q(PCSel_IF));  // open: en, clr
  Comparator #(.mode("unsigned"), .width(1)) comparator_32 (
    .a(Control_WB[1]), .b(1'b1), .eq(comparator_32_eq));  // open: gt, lt
  Comparator #(.mode("unsigned"), .width(5)) comparator_33 (
    .a(Instruction_WB[11:7]), .b({5{1'b0}}), .gt(comparator_33_gt));  // open: eq, lt
  Comparator #(.mode("unsigned"), .width(5)) comparator_34 (
    .a(Instruction_WB[11:7]), .b(Instruction_ID[19:15]), .eq(comparator_34_eq));  // open: gt, lt
  Comparator #(.mode("unsigned"), .width(1)) comparator_35 (
    .a(Control_WB[1]), .b(1'b1), .eq(comparator_35_eq));  // open: gt, lt
  Comparator #(.mode("unsigned"), .width(5)) comparator_36 (
    .a(Instruction_WB[11:7]), .b({5{1'b0}}), .gt(comparator_36_gt));  // open: eq, lt
  Comparator #(.mode("unsigned"), .width(5)) comparator_37 (
    .a(Instruction_WB[11:7]), .b(Instruction_ID[24:20]), .eq(comparator_37_eq));  // open: gt, lt
  and and_6 (WBForward_rs1, comparator_32_eq, comparator_33_gt, comparator_34_eq);
  and and_7 (WBForward_rs2, comparator_35_eq, comparator_36_gt, comparator_37_eq);
  Comparator #(.mode("unsigned"), .width(1)) comparator_38 (
    .a(Control_MEM[1]), .b(1'b1), .eq(comparator_38_eq));  // open: gt, lt
  Comparator #(.mode("unsigned"), .width(5)) comparator_39 (
    .a(Instruction_MEM[11:7]), .b({5{1'b0}}), .gt(comparator_39_gt));  // open: eq, lt
  Comparator #(.mode("unsigned"), .width(5)) comparator_40 (
    .a(Instruction_MEM[11:7]), .b(Instruction_EX[24:20]), .eq(comparator_40_eq));  // open: gt, lt
  partial_store partial_store_1 (
    .Instruction(Instruction_MEM), .MemAddress(MemAddress), .DataFromReg(WriteData_MEM),
    .MemRW(Control_MEM[12]), .MemWriteMask(MemWriteMask), .DataToMem(MemWriteData));
  partial_load partial_load_1 (
    .Instruction(Instruction_MEM), .MemAddress(MemAddress), .DataFromMem(MemReadData), .DataToReg(LoadData));
  and and_8 (Forward_rs2, comparator_38_eq, comparator_39_gt, comparator_40_eq);
  Multiplexer #(.select(2), .width(32)) multiplexer_13 (
    .in0(LoadData), .in1(MemAddress), .in2(NextPC_MEM), .out(WriteBack), .sel(Control_MEM[14:13]));  // open: in3
  Register #(.width(32)) register_16 (.D(WriteBack), .clk(clk), .Q(WriteBack_ID));  // open: en, clr
  Register #(.width(32)) register_17 (.D(Instruction_MEM), .clk(clk), .Q(Instruction_WB));  // open: en, clr
  Register #(.width(15)) register_18 (.D(Control_MEM), .clk(clk), .Q(Control_WB));  // open: en, clr

  // Other names for the same wires on the sheet: ALUResult_MEM[31:0] = MemAddress; PCSel = Control_EX[0];
  //   RegWEn = Control_EX[1]; ImmSel[2:0] = Control_EX[4:2]; Control_EX[11:5] = {ALUSel, BSel, ASel, BrUn};
  //   MemRW = Control_EX[12]; WBSel[1:0] = Control_EX[14:13]; opcode[6:0] = Instruction_ID[6:0];
  //   rd[4:0] = Instruction_ID[11:7]; Instruction_ID (some bits) = {funct7, funct3}; rs1[4:0] = Instruction_ID[19:15];
  //   rs2[4:0] = Instruction_ID[24:20]

  // Notes on the sheet:
  //   BranchTaken
  //   Not Store-type
  //   Not B-type
  //   R-type
  //   R-type
  //   I-type, exclude Load
  //   JALR
  //   Additional Control Logic for Forwarding
  //   Opcode 0b0010011
  //   lui
  //   To IMEM
  //   IMEM (do **NOT** move this)
  //   From IMEM
  //   R-type
  //   I-type, exclude Load
  //   Inputs/Outputs for testing. Do **NOT** move these.
  //   It is OK to move the PC, RegFile, ALU, MEM, Branch Comp, Imm Gen, Partial Load, Partial Store and Control Logic to wherever is most convenient for you when constructing your CPU, and to delete this text
  //   To DMEM
  //   DMEM (do **NOT** move this)
  //   From DMEM
  //   Control Logic Pipelining
  //   Additional Control Logic for Stall
  //   Additional Data Forwarding for WB data
  //   Regfile cannot load the written data in the same cycle
  //   Additional Data Forwarding for Store Data (rs2)
endmodule
