// Logisim project imm-gen.circ as structural Verilog: 1 circuit, main circuit imm_gen
module imm_gen (
  input  [31:0] Instruction,
  input  [2:0] ImmSel,
  output [31:0] Immediate
);

  wire [11:0] Utype;
  wire [31:11] Itype, Stype;
  wire [31:12] Btype;
  wire [31:20] Jtype;

  assign Itype = {{20{Instruction[31]}}, Instruction[31]};  // Bit_Extender bit_extender_1
  assign Stype = {{20{Instruction[31]}}, Instruction[31]};  // Bit_Extender bit_extender_2
  Multiplexer #(.select(3), .width(32)) multiplexer_1 (
    .in0({Itype, Instruction[30:20]}), .in1({Stype, Instruction[30:25], Instruction[11:7]}),
    .in2({Btype, Instruction[7], Instruction[30:25], Instruction[11:8], 1'b0}),
    .in3({Instruction[31:12], Utype}),
    .in4({Jtype, Instruction[19:12], Instruction[20], Instruction[30:21], 1'b0}), .out(Immediate),
    .sel(ImmSel));  // open: in5, in6, in7
  assign Btype = {{19{Instruction[31]}}, Instruction[31]};  // Bit_Extender bit_extender_3
  assign Utype = {{11{1'b0}}, 1'b0};  // Bit_Extender bit_extender_4
  assign Jtype = {{11{Instruction[31]}}, Instruction[31]};  // Bit_Extender bit_extender_5

  // Other names for the same wires on the sheet: Btype[11:1] = {Instruction[7], Instruction[30:25], Instruction[11:8]};
  //   Stype[10:0] = {Instruction[30:25], Instruction[11:7]}; Itype[10:0] = Instruction[30:20];
  //   Jtype[19:1] = {Instruction[19:12], Instruction[20], Instruction[30:21]}; Utype[31:12] = Instruction[31:12]

  // Notes on the sheet:
  //   INPUTS to your circuit
  //   I-type
  //   S-type
  //   DON'T CHANGE THE LOCATIONS OF THE INPUTS AND OUTPUTS!
  //   B-type
  //   U-type
  //   OUTPUT from your circuit
  //   J-type
endmodule
