// Logisim project partial-load.circ as structural Verilog: 1 circuit, main circuit partial_load
module partial_load (
  input  [31:0] Instruction,
  input  [31:0] MemAddress,
  input  [31:0] DataFromMem,
  output [31:0] DataToReg
);

  wire [7:7] multiplexer_1_out;
  wire [15:15] multiplexer_2_out;
  wire [31:0] lbValue, lhValue;

  Multiplexer #(.select(2), .width(8)) multiplexer_1 (
    .in0(DataFromMem[7:0]), .in1(DataFromMem[15:8]), .in2(DataFromMem[23:16]), .in3(DataFromMem[31:24]),
    .out({multiplexer_1_out[7], lbValue[6:0]}), .sel(MemAddress[1:0]));
  Multiplexer #(.select(2), .width(16)) multiplexer_2 (
    .in0(DataFromMem[15:0]), .in1(DataFromMem[23:8]), .in2(DataFromMem[31:16]),
    .out({multiplexer_2_out[15], lhValue[14:0]}), .sel(MemAddress[1:0]));  // open: in3
  assign lbValue[31:7] = {{24{multiplexer_1_out[7]}}, multiplexer_1_out[7]};  // Bit_Extender bit_extender_1
  assign lhValue[31:15] = {{16{multiplexer_2_out[15]}}, multiplexer_2_out[15]};  // Bit_Extender bit_extender_2
  Multiplexer #(.select(2), .width(32)) multiplexer_3 (
    .in0(lbValue), .in1(lhValue), .in2(DataFromMem), .out(DataToReg), .sel(Instruction[13:12]));  // open: in3

  // Notes on the sheet:
  //   INPUTS to your circuit
  //   DON'T CHANGE THE LOCATIONS OF THE INPUTS AND OUTPUTS!
  //   OUTPUT from your circuit
endmodule
