// Logisim project partial-store.circ as structural Verilog: 1 circuit, main circuit partial_store
module partial_store (
  input  [31:0] Instruction,
  input  [31:0] MemAddress,
  input  [31:0] DataFromReg,
  input  MemRW,
  output [3:0] MemWriteMask,
  output [31:0] DataToMem
);

  wire comparator_1_eq, comparator_2_eq, comparator_3_eq, comparator_4_eq, comparator_5_eq, comparator_6_eq,
       comparator_7_eq, comparator_8_eq, comparator_9_eq, comparator_10_eq, comparator_11_eq,
       comparator_12_eq, comparator_13_eq, comparator_14_eq, is_0b0001, is_0b0010, is_0b0011, is_0b0100,
       is_0b1000, is_0b1100, is_0b1111;
  wire [3:0] bit_extender_7_out, priority_encoder_1_out;
  wire [15:0] sh2;
  wire [23:0] sb3;
  wire [31:0] sb1, sb2;
  wire [31:8] sb0;
  wire [31:16] sh0;

  assign sb0 = {{23{1'b0}}, 1'b0};  // Bit_Extender bit_extender_1
  assign {sb1[31:16], sb1[7:0]} = {{23{1'b0}}, 1'b0};  // Bit_Extender bit_extender_2
  assign {sb2[31:24], sb2[15:0]} = {{23{1'b0}}, 1'b0};  // Bit_Extender bit_extender_3
  assign sb3 = {{23{1'b0}}, 1'b0};  // Bit_Extender bit_extender_4
  assign sh0 = {{15{1'b0}}, 1'b0};  // Bit_Extender bit_extender_5
  assign sh2 = {{15{1'b0}}, 1'b0};  // Bit_Extender bit_extender_6
  Comparator #(.mode("unsigned"), .width(3)) comparator_1 (
    .a(Instruction[14:12]), .b(3'b000), .eq(comparator_1_eq));  // open: gt, lt
  Comparator #(.mode("unsigned"), .width(2)) comparator_2 (
    .a(MemAddress[1:0]), .b(2'b00), .eq(comparator_2_eq));  // open: gt, lt
  Comparator #(.mode("unsigned"), .width(3)) comparator_3 (
    .a(Instruction[14:12]), .b(3'b000), .eq(comparator_3_eq));  // open: gt, lt
  Comparator #(.mode("unsigned"), .width(2)) comparator_4 (
    .a(MemAddress[1:0]), .b(2'b01), .eq(comparator_4_eq));  // open: gt, lt
  Comparator #(.mode("unsigned"), .width(3)) comparator_5 (
    .a(Instruction[14:12]), .b(3'b000), .eq(comparator_5_eq));  // open: gt, lt
  Comparator #(.mode("unsigned"), .width(2)) comparator_6 (
    .a(MemAddress[1:0]), .b(2'b10), .eq(comparator_6_eq));  // open: gt, lt
  Comparator #(.mode("unsigned"), .width(3)) comparator_7 (
    .a(Instruction[14:12]), .b(3'b000), .eq(comparator_7_eq));  // open: gt, lt
  Comparator #(.mode("unsigned"), .width(2)) comparator_8 (
    .a(MemAddress[1:0]), .b(2'b11), .eq(comparator_8_eq));  // open: gt, lt
  Comparator #(.mode("unsigned"), .width(3)) comparator_9 (
    .a(Instruction[14:12]), .b(3'b001), .eq(comparator_9_eq));  // open: gt, lt
  Comparator #(.mode("unsigned"), .width(2)) comparator_10 (
    .a(MemAddress[1:0]), .b(2'b00), .eq(comparator_10_eq));  // open: gt, lt
  Comparator #(.mode("unsigned"), .width(3)) comparator_11 (
    .a(Instruction[14:12]), .b(3'b001), .eq(comparator_11_eq));  // open: gt, lt
  Comparator #(.mode("unsigned"), .width(2)) comparator_12 (
    .a(MemAddress[1:0]), .b(2'b10), .eq(comparator_12_eq));  // open: gt, lt
  Comparator #(.mode("unsigned"), .width(3)) comparator_13 (
    .a(Instruction[14:12]), .b(3'b010), .eq(comparator_13_eq));  // open: gt, lt
  Comparator #(.mode("unsigned"), .width(2)) comparator_14 (
    .a(MemAddress[1:0]), .b(2'b00), .eq(comparator_14_eq));  // open: gt, lt
  and and_1 (is_0b0001, comparator_1_eq, comparator_2_eq);
  and and_2 (is_0b0010, comparator_3_eq, comparator_4_eq);
  and and_3 (is_0b0100, comparator_5_eq, comparator_6_eq);
  and and_4 (is_0b1000, comparator_7_eq, comparator_8_eq);
  and and_5 (is_0b0011, comparator_9_eq, comparator_10_eq);
  and and_6 (is_0b1100, comparator_11_eq, comparator_12_eq);
  and and_7 (is_0b1111, comparator_13_eq, comparator_14_eq);
  Priority_Encoder #(.select_enc(4)) priority_encoder_1 (
    .in1(is_0b0001), .in2(is_0b0010), .in3(is_0b0011), .in4(is_0b0100), .in8(is_0b1000), .in12(is_0b1100),
    .in15(is_0b1111), .out(priority_encoder_1_out));  // open: in0, in5, in6, in7, in9, in10, in11, in13, in14, gs, en_out, en_in
  assign bit_extender_7_out = {{3{MemRW}}, MemRW};  // Bit_Extender bit_extender_7
  assign MemWriteMask = priority_encoder_1_out & bit_extender_7_out;  // AND_Gate and_8, 4 bits wide
  Multiplexer #(.select(4), .width(32)) multiplexer_1 (
    .in1({sb0, DataFromReg[7:0]}), .in2({sb1[31:16], DataFromReg[7:0], sb1[7:0]}),
    .in3({sh0, DataFromReg[15:0]}), .in4({sb2[31:24], DataFromReg[7:0], sb2[15:0]}),
    .in8({DataFromReg[7:0], sb3}), .in12({DataFromReg[15:0], sh2}), .in15(DataFromReg), .out(DataToMem),
    .sel(MemWriteMask));  // open: in0, in5, in6, in7, in9, in10, in11, in13, in14

  // Other names for the same wires on the sheet: funct3[2:0] = Instruction[14:12]; bottom2[1:0] = MemAddress[1:0];
  //   sb0[7:0] = DataFromReg[7:0]; sb1[15:8] = DataFromReg[7:0]; sb2[23:16] = DataFromReg[7:0];
  //   sb3[31:24] = DataFromReg[7:0]; sh0[15:0] = DataFromReg[15:0]; sh2[31:16] = DataFromReg[15:0]

  // Notes on the sheet:
  //   INPUTS to your circuit
  //   DON'T CHANGE THE LOCATIONS OF THE INPUTS AND OUTPUTS!
  //   OUTPUT from your circuit
endmodule
