// Logisim project regfile.circ as structural Verilog: 1 circuit, main circuit regfile
module regfile (
  input  [4:0] ReadIndex1,
  input  [4:0] ReadIndex2,
  input  [4:0] WriteIndex,
  input  [31:0] WriteData,
  input  RegWEn,
  input  clk,
  output [31:0] ra,
  output [31:0] sp,
  output [31:0] t0,
  output [31:0] t1,
  output [31:0] t2,
  output [31:0] s0,
  output [31:0] s1,
  output [31:0] a0,
  output [31:0] ReadData1,
  output [31:0] ReadData2
);

  wire WEn_a0, WEn_ra, WEn_s0, WEn_s1, WEn_sp, WEn_t0, WEn_t1, WEn_t2, WEn_x3, WEn_x4, WEn_x11, WEn_x12,
       WEn_x13, WEn_x14, WEn_x15, WEn_x16, WEn_x17, WEn_x18, WEn_x19, WEn_x20, WEn_x21, WEn_x22, WEn_x23,
       WEn_x24, WEn_x25, WEn_x26, WEn_x27, WEn_x28, WEn_x29, WEn_x30, WEn_x31;
  wire [31:0] x3, x4, x11, x12, x13, x14, x15, x16, x17, x18, x19, x20, x21, x22, x23, x24, x25, x26, x27,
       x28, x29, x30, x31;

  Demultiplexer #(.select(5)) demultiplexer_1 (
    .out1(WEn_ra), .out2(WEn_sp), .out3(WEn_x3), .out4(WEn_x4), .out5(WEn_t0), .out6(WEn_t1), .out7(WEn_t2),
    .out8(WEn_s0), .out9(WEn_s1), .out10(WEn_a0), .out11(WEn_x11), .out12(WEn_x12), .out13(WEn_x13),
    .out14(WEn_x14), .out15(WEn_x15), .out16(WEn_x16), .out17(WEn_x17), .out18(WEn_x18), .out19(WEn_x19),
    .out20(WEn_x20), .out21(WEn_x21), .out22(WEn_x22), .out23(WEn_x23), .out24(WEn_x24), .out25(WEn_x25),
    .out26(WEn_x26), .out27(WEn_x27), .out28(WEn_x28), .out29(WEn_x29), .out30(WEn_x30), .out31(WEn_x31),
    .in(RegWEn), .sel(WriteIndex));  // open: out0
  Register #(.width(32)) register_1 (.D(WriteData), .en(WEn_ra), .clk(clk), .Q(ra));  // open: clr
  Register #(.width(32)) register_2 (.D(WriteData), .en(WEn_sp), .clk(clk), .Q(sp));  // open: clr
  Register #(.width(32)) register_3 (.D(WriteData), .en(WEn_t0), .clk(clk), .Q(t0));  // open: clr
  Register #(.width(32)) register_4 (.D(WriteData), .en(WEn_t1), .clk(clk), .Q(t1));  // open: clr
  Register #(.width(32)) register_5 (.D(WriteData), .en(WEn_t2), .clk(clk), .Q(t2));  // open: clr
  Register #(.width(32)) register_6 (.D(WriteData), .en(WEn_s0), .clk(clk), .Q(s0));  // open: clr
  Register #(.width(32)) register_7 (.D(WriteData), .en(WEn_s1), .clk(clk), .Q(s1));  // open: clr
  Register #(.width(32)) register_8 (.D(WriteData), .en(WEn_a0), .clk(clk), .Q(a0));  // open: clr
  Register #(.width(32)) register_9 (.D(WriteData), .en(WEn_x3), .clk(clk), .Q(x3));  // open: clr
  Register #(.width(32)) register_10 (.D(WriteData), .en(WEn_x4), .clk(clk), .Q(x4));  // open: clr
  Register #(.width(32)) register_11 (.D(WriteData), .en(WEn_x11), .clk(clk), .Q(x11));  // open: clr
  Register #(.width(32)) register_12 (.D(WriteData), .en(WEn_x12), .clk(clk), .Q(x12));  // open: clr
  Register #(.width(32)) register_13 (.D(WriteData), .en(WEn_x13), .clk(clk), .Q(x13));  // open: clr
  Register #(.width(32)) register_14 (.D(WriteData), .en(WEn_x14), .clk(clk), .Q(x14));  // open: clr
  Register #(.width(32)) register_15 (.D(WriteData), .en(WEn_x15), .clk(clk), .Q(x15));  // open: clr
  Register #(.width(32)) register_16 (.D(WriteData), .en(WEn_x16), .clk(clk), .Q(x16));  // open: clr
  Register #(.width(32)) register_17 (.D(WriteData), .en(WEn_x17), .clk(clk), .Q(x17));  // open: clr
  Register #(.width(32)) register_18 (.D(WriteData), .en(WEn_x18), .clk(clk), .Q(x18));  // open: clr
  Register #(.width(32)) register_19 (.D(WriteData), .en(WEn_x19), .clk(clk), .Q(x19));  // open: clr
  Register #(.width(32)) register_20 (.D(WriteData), .en(WEn_x20), .clk(clk), .Q(x20));  // open: clr
  Register #(.width(32)) register_21 (.D(WriteData), .en(WEn_x21), .clk(clk), .Q(x21));  // open: clr
  Register #(.width(32)) register_22 (.D(WriteData), .en(WEn_x22), .clk(clk), .Q(x22));  // open: clr
  Register #(.width(32)) register_23 (.D(WriteData), .en(WEn_x23), .clk(clk), .Q(x23));  // open: clr
  Register #(.width(32)) register_24 (.D(WriteData), .en(WEn_x24), .clk(clk), .Q(x24));  // open: clr
  Multiplexer #(.select(5), .width(32)) multiplexer_1 (
    .in0({32{1'b0}}), .in1(ra), .in2(sp), .in3(x3), .in4(x4), .in5(t0), .in6(t1), .in7(t2), .in8(s0),
    .in9(s1), .in10(a0), .in11(x11), .in12(x12), .in13(x13), .in14(x14), .in15(x15), .in16(x16), .in17(x17),
    .in18(x18), .in19(x19), .in20(x20), .in21(x21), .in22(x22), .in23(x23), .in24(x24), .in25(x25),
    .in26(x26), .in27(x27), .in28(x28), .in29(x29), .in30(x30), .in31(x31), .out(ReadData1), .sel(ReadIndex1));
  Register #(.width(32)) register_25 (.D(WriteData), .en(WEn_x25), .clk(clk), .Q(x25));  // open: clr
  Register #(.width(32)) register_26 (.D(WriteData), .en(WEn_x26), .clk(clk), .Q(x26));  // open: clr
  Register #(.width(32)) register_27 (.D(WriteData), .en(WEn_x27), .clk(clk), .Q(x27));  // open: clr
  Register #(.width(32)) register_28 (.D(WriteData), .en(WEn_x28), .clk(clk), .Q(x28));  // open: clr
  Register #(.width(32)) register_29 (.D(WriteData), .en(WEn_x29), .clk(clk), .Q(x29));  // open: clr
  Register #(.width(32)) register_30 (.D(WriteData), .en(WEn_x30), .clk(clk), .Q(x30));  // open: clr
  Register #(.width(32)) register_31 (.D(WriteData), .en(WEn_x31), .clk(clk), .Q(x31));  // open: clr
  Multiplexer #(.select(5), .width(32)) multiplexer_2 (
    .in0({32{1'b0}}), .in1(ra), .in2(sp), .in3(x3), .in4(x4), .in5(t0), .in6(t1), .in7(t2), .in8(s0),
    .in9(s1), .in10(a0), .in11(x11), .in12(x12), .in13(x13), .in14(x14), .in15(x15), .in16(x16), .in17(x17),
    .in18(x18), .in19(x19), .in20(x20), .in21(x21), .in22(x22), .in23(x23), .in24(x24), .in25(x25),
    .in26(x26), .in27(x27), .in28(x28), .in29(x29), .in30(x30), .in31(x31), .out(ReadData2), .sel(ReadIndex2));

  // Notes on the sheet:
  //   INPUTS to your circuit
  //   DON'T CHANGE THE LOCATIONS OF THE INPUTS AND OUTPUTS!
  //   These are DEBUG/TEST outputs from your circuit.
  //   OUTPUTS from your circuit
endmodule
